# Fritzing sketch dht11 (saved by Fritzing 0.9.3b)
breadboards: 1

parts:
  元件1 = Arduino Uno (Rev3)
  DHT11_1 = DHT11 module

nets:
  N1: 元件1.D2, DHT11_1.DATA
  5V: 元件1.5V, DHT11_1.VCC
  GND: 元件1.GND, DHT11_1.GND

custom parts:
  DHT11 module: DHT11 black pcb module
